// Logisim project D-ff.circ as structural Verilog: 1 circuit, main circuit main
module main (
  input  in_1,
  input  C,
  input  nC,
  input  Q0,
  input  nQ0,
  input  Q1,
  input  nQ1,
  input  Q2,
  input  nQ2,
  output out_10,
  output out_11,
  output out_12
);

  wire d_ff_1_qn, d_ff_2_qn, d_ff_3_qn, not_1_out;

  not not_1 (not_1_out, in_1);
  D_Flip_Flop d_ff_1 (.clk(not_1_out), .D(d_ff_1_qn), .Q(out_10), .Qn(d_ff_1_qn));  // open: preset, en, reset
  D_Flip_Flop d_ff_2 (.clk(d_ff_1_qn), .D(d_ff_2_qn), .Q(out_11), .Qn(d_ff_2_qn));  // open: preset, en, reset
  D_Flip_Flop d_ff_3 (.clk(d_ff_2_qn), .D(d_ff_3_qn), .Q(out_12), .Qn(d_ff_3_qn));  // open: preset, en, reset
endmodule
