// Logisim project JK FF.circ as structural Verilog: 1 circuit, main circuit main
module main (
  input  in_1,
  input  in_2,
  input  in_3,
  output out_4,
  output out_5
);

  wire nand_1_out, nand_2_out, nand_3_out, nand_4_out, nand_5_out, nand_6_out, not_1_out;

  nand nand_1 (nand_1_out, out_5, in_1, in_2);
  nand nand_2 (nand_2_out, in_2, in_3, out_4);
  not not_1 (not_1_out, in_2);
  nand nand_3 (nand_3_out, nand_1_out, nand_4_out);
  nand nand_4 (nand_4_out, nand_3_out, nand_2_out);
  nand nand_5 (nand_5_out, nand_3_out, not_1_out);
  nand nand_6 (nand_6_out, not_1_out, nand_4_out);
  nand nand_7 (out_4, nand_5_out, out_5);
  nand nand_8 (out_5, out_4, nand_6_out);
endmodule
